# Fritzing sketch half-adder (saved by Fritzing 0.9.5d)
circuit board: 8.46667cm x 5.64444cm
breadboards: 1

parts:
  IC1-AND = 74HC08 Logic AND Gate [part_number=74HC08 package="DIP (Dual Inline) [THT]"]
  74HC86-XOR = DIP - 14 pins [chip_label=74LS86 package="DIP (Dual Inline) [THT]"]
  SUM = smd LED [color="Red (633nm)" package="1206 [SMD]"]
  CARRY = smd LED [color="Red (633nm)" package="1206 [SMD]"]
  x = Round Pushbutton
  y = Round Pushbutton
  R1 = Resistor [tolerance=±5% resistance=330 package=THT]
  R2 = Resistor [tolerance=±5% resistance=330 package=THT]
  R3 = Resistor [tolerance=±5% resistance=10000 package=THT]
  R4 = Resistor [tolerance=±5% resistance=10000 package=THT]

nets:
  N1: IC1-AND.1A, 74HC86-XOR.A1, x.leg1, R3.Pin_0
  GND: IC1-AND.1B, IC1-AND.GND, 74HC86-XOR.B1, 74HC86-XOR.GND, SUM.cathode, CARRY.cathode, y.leg1, R3.Pin_1, R4.Pin_0, R4.Pin_1
  N2: IC1-AND.1Y, R1.Pin_0
  5V: IC1-AND.VCC, 74HC86-XOR.VCC, x.leg0, y.leg0
  N3: 74HC86-XOR.Y1, R2.Pin_0
  N4: SUM.anode, R2.Pin_1
  N5: CARRY.anode, R1.Pin_1

custom parts:
  DIP - 14 pins: A DIP stand-in part for whatever IC you want. With 14 pins on a 300mil dual inline package (DIP) footprint.
